# Fritzing sketch Troca de energia automática (saved by Fritzing 0.9.3b)
breadboards: 1

parts:
  Componente2 = ACS712 Low Current Sensor Board v12
  U1 = 2ChannelRelay
  Componente1 = Intel Galileo
  BAT1 = BC9VPC [package=bc9vpc]
  BAT2 = BC9VPC [package=bc9vpc]
  LED1 = LED - 5mm [color="Red (633nm)" package="5 mm [THT]"]
  LED2 = LED - 5mm [color="Red (633nm)" package="5 mm [THT]"]
  R1 = Resistor [tolerance=±5% resistance=220 package="0603 [SMD]"]
  R2 = Resistor [tolerance=±5% resistance=220 package="0603 [SMD]"]

nets:
  N1: Componente2.IP+, U1.connector4, BAT1.V+
  5V: Componente2.5V, U1.connector0, Componente1.5V
  N2: Componente2.VO, Componente1.A0
  GND: Componente2.GND, U1.connector1, Componente1.GND
  N3: Componente2.IP-, BAT1.V-, R2.Pin_1
  N4: U1.connector2, Componente1.D2
  N5: U1.connector3, Componente1.D4
  N6: U1.connector6, LED2.cathode, R2.Pin_0
  N7: U1.connector7, BAT2.V+
  N8: U1.connector9, LED1.cathode, R1.Pin_0
  N9: BAT2.V-, R1.Pin_1

notes:
  Energia da Placa Solar
  "Energia da Rua"
